// Logisim project circuito.circ as structural Verilog: 1 circuit, main circuit main
module main (
  input  A,
  input  B,
  input  C,
  input  A_2,
  input  B_2,
  input  C_2,
  output Y,
  output X
);

  wire and_1_out, and_2_out, and_3_out, not_1_out, not_2_out, not_3_out, or_1_out, or_2_out;

  not not_1 (not_1_out, A);
  not not_2 (not_2_out, B_2);
  not not_3 (not_3_out, C);
  or or_1 (or_1_out, A_2, B_2);
  or or_2 (or_2_out, not_2_out, C_2);
  and and_1 (and_1_out, A, C);
  and and_2 (and_2_out, B, not_3_out);
  and and_3 (and_3_out, not_1_out, B, C);
  or or_3 (Y, and_1_out, and_2_out, and_3_out);
  and and_4 (X, or_1_out, or_2_out);

  // Notes on the sheet:
  //   Y = AC + BC' + A'BC
  //   X = (A + B) (B' + C)
endmodule
