// Logisim project circuito.circ as structural Verilog: 1 circuit, main circuit main
module main (
  input  A,
  input  B,
  input  C,
  input  D,
  input  E,
  output S
);

  wire and_1_out, and_2_out, and_3_out, and_4_out, and_5_out, nand_1_out, nor_1_out, not_1_out, not_2_out,
       not_3_out, or_1_out;

  not not_1 (not_1_out, A);
  not not_2 (not_2_out, D);
  not not_3 (not_3_out, E);
  nand nand_1 (nand_1_out, not_1_out, B);
  and and_1 (and_1_out, C, not_2_out);
  and and_2 (and_2_out, A, not_3_out, not_2_out);
  and and_3 (and_3_out, C, D, E);
  nor nor_1 (nor_1_out, nand_1_out, and_1_out);
  or or_1 (or_1_out, and_2_out, and_3_out);
  and and_4 (and_4_out, nor_1_out, E);
  and and_5 (and_5_out, or_1_out, not_1_out);
  or or_2 (S, and_4_out, and_5_out);

  // Notes on the sheet:
  //   ((A'.B)' + (C.D'))'.E + ((A.D'.E') + (C.D.E)).A'
endmodule
