// Logisim project circuito.circ as structural Verilog: 1 circuit, main circuit main
module main (
  input  A,
  input  B,
  input  C,
  input  D,
  output S
);

  wire and_1_out, and_2_out, and_3_out, nand_1_out, nand_2_out, nand_3_out, not_1_out, not_2_out, not_3_out,
       or_1_out, or_2_out, xor_1_out;

  not not_1 (not_1_out, B);
  not not_2 (not_2_out, C);
  not not_3 (not_3_out, D);
  or or_1 (or_1_out, B, not_3_out);
  nand nand_1 (nand_1_out, A, B);
  and and_1 (and_1_out, not_1_out, D);
  and and_2 (and_2_out, or_1_out, A);
  or or_2 (or_2_out, nand_1_out, and_1_out);
  and and_3 (and_3_out, or_2_out, not_2_out);
  xor xor_1 (xor_1_out, and_2_out, and_3_out);
  nand nand_2 (nand_2_out, A, B, C, not_3_out);
  nand nand_3 (nand_3_out, A, B, D);
  or or_3 (S, xor_1_out, nand_2_out, nand_3_out);
endmodule
